// Logisim project Memoria.circ as structural Verilog: 1 circuit, main circuit main
module main (
  input  a8,
  input  a7,
  input  a6,
  input  a5,
  input  a4,
  input  a3,
  input  a2,
  input  a1,
  input  a0,
  input  inh,
  input  inl,
  input  w,
  output outh,
  output outl
);

  wire and_1_out, and_2_out, and_3_out, and_4_out, and_5_out, and_6_out, nor_1_out, nor_2_out, not_1_out,
       or_1_out, or_2_out, or_3_out, or_4_out, or_5_out, or_6_out, or_7_out, or_8_out, or_9_out, or_10_out,
       or_11_out, or_12_out, or_13_out, or_14_out;

  or or_1 (or_1_out, a8, a7);
  or or_2 (or_2_out, a8, a7);
  or or_3 (or_3_out, or_1_out, a6);
  or or_4 (or_4_out, or_3_out, or_5_out);
  or or_5 (or_5_out, a5, a4);
  or or_6 (or_6_out, a3, a2);
  or or_7 (or_7_out, or_6_out, or_8_out);
  or or_8 (or_8_out, a1, a0);
  or or_9 (or_9_out, or_2_out, a6);
  or or_10 (or_10_out, or_9_out, or_11_out);
  or or_11 (or_11_out, a5, a4);
  or or_12 (or_12_out, a3, a2);
  or or_13 (or_13_out, or_12_out, or_14_out);
  or or_14 (or_14_out, a1, a0);
  nor nor_1 (nor_1_out, or_4_out, or_7_out);
  nor nor_2 (nor_2_out, or_10_out, or_13_out);
  not not_1 (not_1_out, inh);
  and and_1 (and_1_out, nor_1_out, inl);
  and and_2 (and_2_out, nor_2_out, not_1_out);
  and and_3 (and_3_out, and_1_out, w);
  and and_4 (and_4_out, inh, w);
  and and_5 (and_5_out, and_2_out, w);
  and and_6 (and_6_out, inl, w);
  or or_15 (outh, and_3_out, and_4_out);
  or or_16 (outl, and_5_out, and_6_out);
endmodule
